// Logisim project 1 bit comparator.circ as structural Verilog
module _1_bit_comparator (
  input  in_1,
  input  in_2,
  output out_3,
  output out_4,
  output out_5
);

  wire not_1_out, not_3_out, xor_1_out;

  not not_1 (not_1_out, in_1);
  and and_1 (out_5, not_1_out, in_2);
  xor xor_1 (xor_1_out, in_2, in_1);
  not not_2 (out_4, xor_1_out);
  not not_3 (not_3_out, in_2);
  and and_2 (out_3, in_1, not_3_out);
endmodule
