// Logisim project Adder 2LineMux 4LineMux 1 Bit Alu.circ as structural Verilog
module Adder (
  input  A,
  input  B,
  input  C,
  output SUM,
  output CARRY
);

  wire and_1_out, and_2_out, xor_1_out;

  xor xor_1 (xor_1_out, A, B);
  and and_1 (and_1_out, xor_1_out, C);
  and and_2 (and_2_out, A, B);
  xor xor_2 (SUM, xor_1_out, C);
  or or_1 (CARRY, and_1_out, and_2_out);
endmodule

module _2LineMux (
  input  CONTROL,
  input  A,
  input  B,
  output out_4
);

  wire and_1_out, and_2_out, not_1_out;

  not not_1 (not_1_out, CONTROL);
  and and_1 (and_1_out, not_1_out, A);
  and and_2 (and_2_out, CONTROL, B);
  or or_1 (out_4, and_1_out, and_2_out);
endmodule

module _4LineMux (
  input  in_1,
  input  CONTROL,
  input  A,
  input  B,
  input  C,
  input  D,
  output out_7
);

  wire and_1_out, and_2_out, and_3_out, and_4_out, not_1_out, not_2_out, not_3_out, not_4_out;

  not not_1 (not_1_out, in_1);
  not not_2 (not_2_out, CONTROL);
  not not_3 (not_3_out, in_1);
  not not_4 (not_4_out, CONTROL);
  and and_1 (and_1_out, not_1_out, not_2_out, A);
  and and_2 (and_2_out, not_3_out, CONTROL, B);
  and and_3 (and_3_out, in_1, not_4_out, C);
  and and_4 (and_4_out, in_1, CONTROL, D);
  or or_1 (out_7, and_1_out, and_2_out, and_3_out, and_4_out);
endmodule

module _1bitalu (
  input  Cin,
  input  in_2,
  input  control,
  input  A,
  input  in_5,
  output OUTPUT,
  output COUT
);

  wire adder_1_sum, and_1_out, n2linemux_1_out_4, not_1_out, or_1_out;

  not not_1 (not_1_out, in_5);
  _2LineMux u_2linemux_1 (.A(in_5), .B(not_1_out), .out_4(n2linemux_1_out_4), .CONTROL(control));
  Adder adder_1 (.A(Cin), .B(A), .C(n2linemux_1_out_4), .SUM(adder_1_sum), .CARRY(COUT));
  and and_1 (and_1_out, A, in_5);
  or or_1 (or_1_out, A, in_5);
  _4LineMux u_4linemux_1 (
    .A(and_1_out), .B(or_1_out), .C(adder_1_sum), .D(adder_1_sum), .out_7(OUTPUT), .in_1(in_2),
    .CONTROL(control));
endmodule
