// Logisim project HalfAdder 2 Compliment Inventor.circ as structural Verilog: 4 circuits, main circuit main
module main (
  input  B,
  input  A,
  input  in_3,
  input  in_4,
  input  in_5,
  input  in_6,
  input  in_7,
  output A___B,
  output A___B_2,
  output A___B_3,
  output out_11,
  output out_12,
  output out_13,
  output out_14
);

  wire half_adder_2_carry, half_adder_3_carry, n1_bit_2_compliment_1_output, n1_bit_2_compliment_2_output,
       not_1_out, not_2_out, xor_1_out, xor_2_out, xor_3_out;

  not not_1 (not_1_out, B);
  and and_1 (A___B, not_1_out, n1_bit_2_compliment_1_output);
  _1_BIT_2_COMPLIMENT u_1_bit_2_compliment_1 (
    .CONTROL(in_3), .\input (A), .OUTPUT(n1_bit_2_compliment_1_output));  // open: CARRY
  nor nor_1 (A___B_2, A___B, A___B_3);
  xor xor_1 (xor_1_out, in_4, in_5);
  half_adder half_adder_1 (.A(half_adder_2_carry), .B(xor_1_out), .SUM(out_11), .CARRY(out_12));
  xor xor_2 (xor_2_out, in_4, in_6);
  half_adder half_adder_2 (.A(half_adder_3_carry), .B(xor_2_out), .SUM(out_13), .CARRY(half_adder_2_carry));
  _1_BIT_2_COMPLIMENT u_1_bit_2_compliment_2 (
    .CONTROL(in_3), .\input (B), .OUTPUT(n1_bit_2_compliment_2_output));  // open: CARRY
  not not_2 (not_2_out, A);
  and and_2 (A___B_3, n1_bit_2_compliment_2_output, not_2_out);
  xor xor_3 (xor_3_out, in_4, in_7);
  half_adder half_adder_3 (.A(in_4), .B(xor_3_out), .SUM(out_14), .CARRY(half_adder_3_carry));
endmodule

module half_adder (
  input  A,
  input  B,
  output SUM,
  output CARRY
);

  xor xor_1 (SUM, A, B);
  and and_1 (CARRY, A, B);
endmodule

module _2_compliment_inventor (
  input  in_1,
  input  in_2,
  input  in_3,
  input  in_4,
  output out_5,
  output out_6,
  output out_7,
  output out_8
);

  wire half_adder_2_carry, half_adder_3_carry, xor_1_out, xor_2_out, xor_3_out;

  xor xor_1 (xor_1_out, in_1, in_2);
  half_adder half_adder_1 (.A(half_adder_2_carry), .B(xor_1_out), .SUM(out_6), .CARRY(out_5));
  xor xor_2 (xor_2_out, in_1, in_3);
  half_adder half_adder_2 (.A(half_adder_3_carry), .B(xor_2_out), .SUM(out_7), .CARRY(half_adder_2_carry));
  xor xor_3 (xor_3_out, in_1, in_4);
  half_adder half_adder_3 (.A(in_1), .B(xor_3_out), .SUM(out_8), .CARRY(half_adder_3_carry));
endmodule

module _1_BIT_2_COMPLIMENT (
  input  \input ,
  input  CONTROL,
  output CARRY,
  output OUTPUT
);

  wire xor_1_out;

  xor xor_1 (xor_1_out, CONTROL, \input );
  half_adder half_adder_1 (.A(CONTROL), .B(xor_1_out), .SUM(OUTPUT), .CARRY(CARRY));
endmodule
