// Logisim project adder.circ as structural Verilog
module my_own_adder (
  input  A,
  input  B,
  input  A_2,
  input  B_2,
  output SUM,
  output CARRY,
  output SUM_2,
  output CARRY_2
);

  xor xor_1 (SUM, A, B);
  and and_1 (CARRY, A, B);
  xor xor_2 (SUM_2, A_2, B_2);
  and and_2 (CARRY_2, A_2, B_2);
endmodule
