// Logisim project adders different style.circ as structural Verilog: 1 circuit, main circuit main
module main (
  input  A,
  input  B,
  input  C,
  input  A_2,
  input  B_2,
  input  C_2,
  output SUM,
  output CARRY_OUT,
  output SUM_2,
  output CARRY_OUT_2
);

  wire and_1_out, and_2_out, and_3_out, and_4_out, and_5_out, not_1_out, not_2_out, or_1_out, xor_1_out,
       xor_2_out;

  not not_1 (not_1_out, A_2);
  not not_2 (not_2_out, B_2);
  and and_1 (and_1_out, not_1_out, B_2, C_2);
  and and_2 (and_2_out, A_2, not_2_out, C_2);
  and and_3 (and_3_out, A_2, B_2);
  xor xor_1 (xor_1_out, A, B);
  xor xor_2 (xor_2_out, A_2, B_2);
  and and_4 (and_4_out, xor_1_out, C);
  and and_5 (and_5_out, A, B);
  xor xor_3 (SUM_2, xor_2_out, C_2);
  or or_1 (or_1_out, and_1_out, and_2_out);
  or or_2 (CARRY_OUT_2, or_1_out, and_3_out);
  xor xor_4 (SUM, xor_1_out, C);
  or or_3 (CARRY_OUT, and_4_out, and_5_out);
endmodule
