// Logisim project multiplexer.circ as structural Verilog: 1 circuit, main circuit main
module main (
  input  line_0,
  input  line1,
  input  line2,
  input  line_3,
  output x,
  output y,
  output validation
);

  wire and_1_out;

  and and_1 (and_1_out, line1, line2);
  or or_1 (x, line2, line_3);
  or or_2 (y, and_1_out, line_3);
  or or_3 (validation, line_0, line1, line2, line_3);
endmodule
